# Fritzing sketch shema-fritzing (saved by Fritzing 0.9.3b)
breadboards: 1

parts:
  MBED1 = mbed
  S1 = Pushbutton [package="[SMD]"]
  S2 = Pushbutton [package="[SMD]"]
  S3 = Pushbutton [package="[SMD]"]
  S4 = Pushbutton [package="[SMD]"]
  S5 = Pushbutton [package="[SMD]"]
  R1 = Resistor [tolerance=±5% resistance=220 package="0805 [SMD]"]
  R2 = Resistor [tolerance=±5% resistance=220 package="0805 [SMD]"]
  R3 = Resistor [tolerance=±5% resistance=220 package="0805 [SMD]"]
  R4 = Resistor [tolerance=±5% resistance=220 package="0805 [SMD]"]
  R5 = Resistor [tolerance=±5% resistance=220 package=THT]
  Nokia_5110_LCD_Module1 = Nokia 5110 LCD

nets:
  N1: MBED1.GND, R1.Pin_0, R2.Pin_0, R3.Pin_0, R4.Pin_0, R5.Pin_0, Nokia_5110_LCD_Module1.LED, Nokia_5110_LCD_Module1.LED_(out)
  N2: MBED1.pin21, S5.Pin_3, S5.Pin_4, R4.Pin_1
  N3: MBED1.pin22, S4.Pin_3, S4.Pin_4, R5.Pin_1
  N4: MBED1.pin23, S3.Pin_3, S3.Pin_4, R3.Pin_1
  N5: MBED1.pin24, S2.Pin_3, S2.Pin_4, R2.Pin_1
  N6: MBED1.pin25, S1.Pin_3, S1.Pin_4, R1.Pin_1
  N7: MBED1.pin26, Nokia_5110_LCD_Module1.VCC
  N8: MBED1.pin27, Nokia_5110_LCD_Module1.SCLK
  N9: MBED1.pin28, Nokia_5110_LCD_Module1.D/C
  N10: MBED1.pin29, Nokia_5110_LCD_Module1.RST
  N11: MBED1.pin30, Nokia_5110_LCD_Module1.SCE
  N12: MBED1.D+, Nokia_5110_LCD_Module1.GND
  N13: MBED1.VOUT, S1.Pin_1, S1.Pin_2, S2.Pin_1, S2.Pin_2, S3.Pin_1, S3.Pin_2, S4.Pin_1, S4.Pin_2, S5.Pin_1, S5.Pin_2, Nokia_5110_LCD_Module1.DN(MOSI)

custom parts:
  Nokia 5110 LCD: Nokia 5110 Graphic 84*48 LCD module such as the Sparkfun LCD-10168 or the clones from Ebay. There is example code for the Arduino available from the Sparkfun site in https://learn.sparkfun.com/tutorials/graphic-lcd-hookup-guide This is a 3.3V device, if you are running it from a 5V micro you need a 5V tolorant level translator such as the 74ahc367 to protect the signal imputs. Rafa G. did a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
